# Fritzing sketch Arduino amplification with resistor and four LEDs (saved by Fritzing 0.9.3b)
breadboards: 1

parts:
  PCB1 = Arduino Shield PCB  # not connected
  Arduino1 = Arduino Uno (Rev3)
  LED2 = LED - 5mm [color="Blue (525nm)" package="5 mm [THT]"]
  R1 = Resistor [tolerance=±5% resistance=220 package=THT]
  R2 = Resistor [tolerance=±5% resistance=220 package=THT]
  R3 = Resistor [tolerance=±5% resistance=100 package=THT]
  LED3 = LED - 5mm [color="Red (633nm)" package="5 mm [THT]"]
  R4 = Resistor [tolerance=±5% resistance=220 package=THT]
  LED4 = LED - 5mm [color="Green (570nm)" package="5 mm [THT]"]
  R5 = Resistor [tolerance=±5% resistance=220 package=THT]
  LED5 = LED - 5mm [color="Red (633nm)" package="5 mm [THT]"]
  Q1 = NPN-Transistor [package="TO92 [THT]"]

nets:
  N1: Arduino1.D13/SCK, R3.Pin_1
  N2: Arduino1.5V, R1.Pin_1, R2.Pin_1, R4.Pin_1, R5.Pin_1
  N3: Arduino1.GND, Q1.E
  N4: LED2.cathode, LED3.cathode, LED4.cathode, LED5.cathode, Q1.C
  N5: LED2.anode, R1.Pin_0
  N6: R2.Pin_0, LED3.anode
  N7: R3.Pin_0, Q1.B
  N8: R4.Pin_0, LED4.anode
  N9: R5.Pin_0, LED5.anode

notes:
  BLINK

custom parts:
  Arduino Shield PCB: Plain PCB Shaped to fit an Arduino "Shield"

// code stored in the sketch: Blink.ino
/*
  Blink
  
  Switching a LED on and off
  
  This example is part of the Fritzing Creator Kit: www.fritzing.org/creator-kit.
*/

int transistorPin = 13;							 // Transistor

void setup() {                  			// the setup() method is executed only once
  pinMode(transistorPin, OUTPUT);    // Output for transistor
}

void loop() {                   			// the loop() method is repeated
  boolean isOn = false;
	if (isOn) {
		digitalWrite(transistorPin, LOW); // Turn all LEDs off
		isOn = false;
	} else {
		digitalWrite(transistorPin, HIGH); // Turn all LEDS on
		isOn = true;
  }
}
