# Fritzing sketch Arduino blink LED (saved by Fritzing 0.9.3b)
circuit board: 6.88566cm x 5.36311cm

parts:
  LED = LED - 5mm [color="Red (633nm)" package="5 mm [THT]"]
  PCB1 = Arduino Shield PCB  # not connected
  Arduino1 = Arduino Uno (Rev3)

nets:
  N1: LED.cathode, Arduino1.GND
  N2: LED.anode, Arduino1.D13/SCK

notes:
  BLINK

custom parts:
  Arduino Shield PCB: Plain PCB Shaped to fit an Arduino "Shield"

// code stored in the sketch: Blink.ino
/*
  Blink
  
  Switching a LED on and off
  
  This example is part of the Fritzing Creator Kit: www.fritzing.org/creator-kit.
*/

int led = 13;                   // integer variable led is declared

void setup() {                  // the setup() method is executed only once
  pinMode(led, OUTPUT);         // the led PIN is declared as digital output
}

void loop() {                   // the loop() method is repeated
	for (int i=0; i < 3; i++) {
 	 	digitalWrite(led, HIGH);      // switching on the led 
  		delay(300);                  // stopping the program for 1000 milliseconds
  		digitalWrite(led, LOW);       // switching off the led 
  		delay(300);                  // stopping the program for 1000 milliseconds
  }
}
