# Fritzing sketch Arduino blink two LEDs (saved by Fritzing 0.9.3b)
breadboards: 1

parts:
  PCB1 = Arduino Shield PCB  # not connected
  Arduino1 = Arduino Uno (Rev3)
  LED1 = LED - 5mm [color="Red (633nm)" package="5 mm [THT]"]
  LED2 = LED - 5mm [color="Blue (525nm)" package="5 mm [THT]"]
  R1 = Resistor [tolerance=±5% resistance=220 package=THT]
  R2 = Resistor [tolerance=±5% resistance=220 package=THT]

nets:
  N1: Arduino1.D10_PWM/SS, R2.Pin_1
  N2: Arduino1.D11_PWM/MOSI, R1.Pin_1
  N3: Arduino1.GND, LED1.cathode, LED2.cathode
  N4: LED1.anode, R1.Pin_0
  N5: LED2.anode, R2.Pin_0

notes:
  BLINK

custom parts:
  Arduino Shield PCB: Plain PCB Shaped to fit an Arduino "Shield"

// code stored in the sketch: Blink.ino
/*
  Blink
  
  Switching a LED on and off
  
  This example is part of the Fritzing Creator Kit: www.fritzing.org/creator-kit.
*/

int ledPin1 = 10;               // Blue LED
int ledPin2 = 11;							 // Red LED

void setup() {                  // the setup() method is executed only once
  pinMode(ledPin1, OUTPUT);     // Output for blue LED
  pinMode(ledPin2, OUTPUT);			 // Output for red LED
}

void loop() {                   // the loop() method is repeated
	digitalWrite(ledPin1, HIGH);  // switching on blue LED 
  digitalWrite(ledPin2, HIGH);  // switching on red LED  	
  delay(300);                  // stopping the program for 1000 milliseconds
	digitalWrite(ledPin1, LOW);  // switching off blue LED 
  digitalWrite(ledPin2, LOW);  // switching off red LED
  	delay(300);                  // stopping the program for 1000 millisecond
}
