# Fritzing sketch Arduino two LEDs and a button (saved by Fritzing 0.9.3b)
breadboards: 1

parts:
  PCB1 = Arduino Shield PCB  # not connected
  Arduino1 = Arduino Uno (Rev3)
  LED1 = LED - 5mm [color="Red (633nm)" package="5 mm [THT]"]
  LED2 = LED - 5mm [color="Blue (525nm)" package="5 mm [THT]"]
  R1 = Resistor [tolerance=±5% resistance=220 package=THT]
  R2 = Resistor [tolerance=±5% resistance=220 package=THT]
  S1 = Pushbutton [package=THT]
  R3 = Resistor [tolerance=±5% resistance=100 package=THT]

nets:
  N1: Arduino1.D10_PWM/SS, R2.Pin_1
  N2: Arduino1.D11_PWM/MOSI, R1.Pin_1
  N3: Arduino1.GND, LED1.cathode, LED2.cathode, R3.Pin_1
  N4: Arduino1.D3_PWM, S1.leg1, R3.Pin_0
  N5: Arduino1.5V, S1.leg0
  N6: LED1.anode, R1.Pin_0
  N7: LED2.anode, R2.Pin_0

notes:
  BLINK

custom parts:
  Arduino Shield PCB: Plain PCB Shaped to fit an Arduino "Shield"

// code stored in the sketch: Blink.ino
/*
  Blink
  
  Switching a LED on and off
  
  This example is part of the Fritzing Creator Kit: www.fritzing.org/creator-kit.
*/

int ledPin1 = 10;               // Blue LED
int ledPin2 = 11;							 // Red LED
int buttonPin = 3;							 // Button

void setup() {                  // the setup() method is executed only once
  pinMode(ledPin1, OUTPUT);     // Output for blue LED
  pinMode(ledPin2, OUTPUT);			 // Output for red LED
  pinMode(buttonPin, INPUT);    // Input for button
}

void loop() {                   // the loop() method is repeated
  if (digitalRead(buttonPin) == HIGH) {
		digitalWrite(ledPin1, HIGH);  // switching on blue LED 
 	  digitalWrite(ledPin2, LOW);  // switching off red LED 
  } 	else {
		digitalWrite(ledPin1, LOW);  // switching off blue LED 
  		digitalWrite(ledPin2, HIGH);  // switching on red LED
  }
}
