# Fritzing sketch Basic LED (saved by Fritzing 0.9.3b)
breadboards: 1

parts:
  VCC1 = Battery
  S1 = Pushbutton [package="[THT]"]
  R1 = Resistor [tolerance=±5% resistance=220 package=THT]
  LED1 = LED - 5mm [color="Red (633nm)" package="5 mm [THT]"]

nets:
  N1: VCC1.-, S1.Pin_1, S1.Pin_2
  N2: VCC1.+, LED1.cathode
  N3: S1.Pin_3, S1.Pin_4, R1.Pin_1
  N4: R1.Pin_0, LED1.anode
